# Fritzing sketch PirCam_TelegramBot_ESPCAM (saved by Fritzing 0.9.6b)
# 18650 Li-ion Battery: CC-BY Dr Kristofer Chan, King's College London/Remote-research.org
breadboards: 1

parts:
  ESP32_-_Back1 = ESP32 - CAM
  Componente1 = HC-SR501 Body Sensor Module
  Mod1 = TP4056 [part_number=TP4056]
  M1 = MT3608 Module
  BAT1 = 18650 Li-ion Battery [package=battery-18650]
  R1 = Resistor [tolerance=±5% resistance=10 package="0805 [SMD]"]
  R2 = Resistor [tolerance=±5% resistance=10 package="0805 [SMD]"]
  J1 = Power Jack [package=power_jack_smd]
  S5 = Momentary Switch [package=ksa_sealed_tac_switch]
  LED1 = smd LED [color="Red (633nm)" package="0805 [SMD]"]
  R3 = Resistor [tolerance=±5% power=0.25 resistance=100 package=THT]
  S6 = SWITCH-DPDT [package=os]
  R5 = Resistor [tolerance=±5% power=0.25 resistance=10k package=THT]

nets:
  N1: ESP32_-_Back1.GPIO13, Componente1.OUT, R5.Pin_0
  N2: ESP32_-_Back1.GPIO12, R3.Pin_0
  N3: ESP32_-_Back1.GND#7, Componente1.GND, M1.pin4, R1.Pin_0, LED1.cathode, R5.Pin_1
  5V: ESP32_-_Back1.5V, Componente1.VCC, S5.1, S5.2
  N4: Mod1.pin1, J1.GNDBREAK, S6.4
  N5: Mod1.pin2, J1.GND
  N6: Mod1.pin3, S6.1, S6.6
  N7: Mod1.pin4, BAT1.+
  N8: Mod1.pin5, BAT1.-
  N9: Mod1.pin6, M1.pin1
  N10: M1.pin2, S6.5
  N11: M1.pin3, S5.3, S5.4
  N12: R1.Pin_1, R2.Pin_1
  N13: R2.Pin_0, S6.2
  N14: LED1.anode, R3.Pin_1

notes:
  Soldar al GPIO33 luego de eliminar su LED integrado.

custom parts:
  ESP32 - CAM: The ESP32-CAM has a very competitive small-size camera module that can operate independently as a minimum system with a footprint of only 27*40.5*4.5mm and a deep sleep current of up to 6mA.
  HC-SR501 Body Sensor Module: Pyroelectric Infrared PIR Motion Sensor Detector Module
  TP4056: TP4056 Lithium battery charger / protection module. (this one has the pins on .1 boundaried unlike the original)
  MT3608 Module: MT3608 Boost Converter Module Links: Aerosemi MT3608 2A Step Up Converter datasheet
  18650 Li-ion Battery: 18650 li-ion Battery Standard 18650 battery with interactive connectors Creative Common Attribution 4.0 International (CC-BY 4.0) license. Any use of this part requires attribution of Dr Kristofer Chan, Department of Geography, King's College London. Contact kristofer.chan [at] kcl.ac.uk OR kris [at] remote-research.org for further information.
